# Fritzing sketch base_wiring (saved by Fritzing 0.9.3b)
breadboards: 1

parts:
  Part1 = Arduino Uno (Rev3)
  R1 = Photocell (LDR) [package=THT]
  R2 = Resistor [tolerance=±5% resistance=10k package=THT]
  S1 = Pushbutton [package="[THT]"]
  R3 = Resistor [tolerance=±5% resistance=10k package=THT]
  LED1 = LED - 5mm [color="Red (633nm)" package="5 mm [THT]"]
  LED2 = LED - 5mm [color="Green (565nm)" package="5 mm [THT]"]
  R4 = Resistor [tolerance=±5% resistance=10k package=THT]
  R5 = Resistor [tolerance=±5% resistance=10k package=THT]
  J1 = Piezo Speaker
  LED3 = LED - 5mm [color="Red (633nm)" package="5 mm [THT]"]
  R6 = Resistor [tolerance=±5% resistance=10k package=THT]

nets:
  N1: Part1.A0, R1.pin_1, R2.Pin_1
  N2: Part1.D2, LED2.anode
  N3: Part1.D3_PWM, LED1.anode
  N4: Part1.D4, LED3.anode
  N5: Part1.D6_PWM, J1.pin2
  N6: Part1.D7, S1.Pin_3, S1.Pin_4, R3.Pin_1
  N7: Part1.5V, R1.pin_0, S1.Pin_1, S1.Pin_2
  N8: Part1.GND, R2.Pin_0, R3.Pin_0, R4.Pin_0, R5.Pin_0, J1.pin1, R6.Pin_1
  N9: LED1.cathode, R4.Pin_1
  N10: LED2.cathode, R5.Pin_1
  N11: LED3.cathode, R6.Pin_0

notes:
  Calico Home Security System
  - BASE MODEL -
